# Fritzing sketch arduino opstelling (saved by Fritzing 0.9.1b)
breadboards: 1

parts:
  Onderdeel1 = Arduino Uno (Rev3)
  LCD1 = LCD screen
  R1 = Rotary Potentiometer (Large) [maximum_resistance=100kΩ package=THT]
  S1 = Pushbutton [package="[SMD]"]
  S2 = Pushbutton [package="[SMD]"]
  S3 = Pushbutton [package="[SMD]"]
  S4 = Pushbutton [package="[SMD]"]
  R2 = Resistor [tolerance=±5% resistance=220 package=THT]
  R6 = Resistor [tolerance=±5% resistance=220 package=THT]
  R7 = Resistor [tolerance=±5% resistance=220 package=THT]
  R8 = Resistor [tolerance=±5% resistance=220 package=THT]
  J1 = Piezo Speaker
  LED1 = smd LED [color="Red (633nm)" package="0603 [SMD]"]
  R9 = Resistor [tolerance=±5% resistance=220 package=THT]

nets:
  N1: Onderdeel1.D8, LCD1.E
  N2: Onderdeel1.D9_PWM, LCD1.DB4
  N3: Onderdeel1.D10_PWM/SS, LCD1.DB5
  N4: Onderdeel1.D11_PWM/MOSI, LCD1.DB6
  N5: Onderdeel1.D12/MISO, LCD1.DB7
  N6: Onderdeel1.D13/SCK, LED1.anode
  N7: Onderdeel1.D2, S4.Pin_3, S4.Pin_4, R8.Pin_1
  N8: Onderdeel1.D3_PWM, S3.Pin_3, S3.Pin_4, R7.Pin_1
  N9: Onderdeel1.D4, S2.Pin_3, S2.Pin_4, R6.Pin_1
  N10: Onderdeel1.D5_PWM, S1.Pin_3, S1.Pin_4, R2.Pin_1
  N11: Onderdeel1.D6_PWM, J1.pin2
  N12: Onderdeel1.D7, LCD1.RS
  N13: Onderdeel1.5V, LCD1.LED+, R1.leg1, S1.Pin_1, S1.Pin_2, S2.Pin_1, S2.Pin_2, S3.Pin_1, S3.Pin_2, S4.Pin_1, S4.Pin_2
  N14: Onderdeel1.GND, LCD1.R/W, LCD1.LED-, R1.leg2, R2.Pin_0, R6.Pin_0, R7.Pin_0, R8.Pin_0, J1.pin1, R9.Pin_0
  N15: LCD1.V0, R1.wiper
  N16: LED1.cathode, R9.Pin_1
